# Fritzing sketch wireless pir (saved by Fritzing 0.9.2b)
circuit board: 10cm x 6cm
perfboards: 1

parts:
  Part1 = Arduino Pro Mini v13
  PIR1 = PIR sensor
  Part2 = Breadboard Power Supply Board SMD
  U1 = ESP8266 WiFi Module [part_number=ESP8266]
  R1 = Resistor [tolerance=±5% resistance=10k package="0805 [SMD]"]

nets:
  VCC: Part1.VCC, PIR1.VDD, R1.Pin_1
  GND: Part1.GND, PIR1.GND, Part2.GND, U1.GND
  N1: Part1.D13/SCK, PIR1.SIG
  N2: Part1.D8, U1.TXD
  N3: Part1.D7, U1.RXD
  N4: Part1.D6_PWM, U1.RST
  VCC_2: Part2.VCC, U1.VCC
  N5: U1.CH_PD, R1.Pin_0

custom parts:
  ESP8266 WiFi Module: Generic WiFi Module based on the ESP8266 with onboard PCB antenna and UART communications
